// Logisim project test2.circ as structural Verilog: 4 circuits, main circuit main
module main (
  input  FSM_Input,
  output FSM_Output
);

  wire clock_1_out;
  wire [1:0] fsmlogic_1_next_state, register_1_q;

  FSMLogic fsmlogic_1 (
    .Input(FSM_Input), .Current_State(register_1_q), .Output(FSM_Output), .Next_State(fsmlogic_1_next_state));
  Clock clock_1 (.out(clock_1_out));
  Register #(.width(2)) register_1 (.D(fsmlogic_1_next_state), .Q(register_1_q), .clk(clock_1_out));  // open: en, clr
endmodule

module FSMLogic (
  input  Input,
  input  [1:0] Current_State,
  output Output,
  output [1:0] Next_State
);

  wire and_1_out, and_2_out, not_1_out, not_2_out, not_3_out;

  not not_1 (not_1_out, Input);
  not not_2 (not_2_out, Current_State[0]);
  not not_3 (not_3_out, Current_State[1]);
  and and_1 (and_1_out, Input, not_3_out);
  and and_2 (and_2_out, not_1_out, not_2_out);
  or or_1 (Output, and_1_out, and_2_out);
  StateBitZero statebitzero_1 (
    .Input(Input), .State_Bit_0(Current_State[0]), .State_Bit_1(Current_State[1]), .out_4(Next_State[0]));
  StateBitOne statebitone_1 (
    .Input(Input), .State_Bit_0(Current_State[0]), .State_Bit_1(Current_State[1]), .New_State_1(Next_State[1]));
endmodule

module StateBitOne (
  input  Input,
  input  State_Bit_0,
  input  State_Bit_1,
  output New_State_1
);

  wire and_1_out, and_2_out, not_2_out, not_3_out;

  // NOT_Gate not_1 has open pins: in=Input, out=open
  not not_2 (not_2_out, State_Bit_0);
  not not_3 (not_3_out, State_Bit_1);
  and and_1 (and_1_out, Input, not_2_out, not_3_out);
  and and_2 (and_2_out, Input, State_Bit_0, not_3_out);
  nor nor_1 (New_State_1, and_1_out, and_1_out, and_2_out, and_2_out);

  // Notes on the sheet:
  //   PUT CIRCUITRY HERE
endmodule

module StateBitZero (
  input  Input,
  input  State_Bit_0,
  input  State_Bit_1,
  output out_4
);

  wire and_1_out, and_2_out, not_2_out, not_3_out;

  // NOT_Gate not_1 has open pins: in=Input, out=open
  not not_2 (not_2_out, State_Bit_0);
  not not_3 (not_3_out, State_Bit_1);
  and and_1 (and_1_out, Input, not_2_out, not_3_out);
  and and_2 (and_2_out, Input, State_Bit_0, not_3_out);
  nor nor_1 (out_4, and_1_out, and_1_out, and_2_out, and_2_out);

  // Notes on the sheet:
  //   PUT CIRCUITRY HERE
endmodule
